# Fritzing sketch SoundBox (saved by Fritzing 0.9.3b)
circuit board: 8.54826cm x 6.25635cm
breadboards: 1

parts:
  Part1 = Arduino Nano (Rev3.0)
  U1 = 74HC4051 [package=so16]
  microSD1 = MicroSD Card Module
  U2 = 74HC4051 [package=so16]
  S1 = Pushbutton [package="[THT]"]
  LED1 = LED - 3mm [color="Red (633nm)" package="3 mm [THT]"]
  S2 = Pushbutton [package="[THT]"]
  LED2 = LED - 3mm [color="Red (633nm)" package="3 mm [THT]"]
  S3 = Pushbutton [package="[THT]"]
  LED3 = LED - 3mm [color="Red (633nm)" package="3 mm [THT]"]
  S4 = Pushbutton [package="[THT]"]
  LED4 = LED - 3mm [color="Red (633nm)" package="3 mm [THT]"]
  S5 = Pushbutton [package="[THT]"]
  LED5 = LED - 3mm [color="Red (633nm)" package="3 mm [THT]"]
  S6 = Pushbutton [package="[THT]"]
  LED6 = LED - 3mm [color="Red (633nm)" package="3 mm [THT]"]
  S7 = Pushbutton [package="[THT]"]
  LED7 = LED - 3mm [color="Red (633nm)" package="3 mm [THT]"]
  S8 = Pushbutton [package="[THT]"]
  LED8 = LED - 3mm [color="Red (633nm)" package="3 mm [THT]"]
  SP1 = SPEAKER [package=pcb_mount_speaker]

nets:
  GND: Part1.GND, U1.VEE, U1.VSS, microSD1.GND, U2.VEE, U2.VSS, LED1.cathode, LED2.cathode, LED3.cathode, LED4.cathode, LED5.cathode, LED6.cathode, LED7.cathode, LED8.cathode, SP1.+
  N1: Part1.D2, U1.A, U2.A
  N2: Part1.D3, U1.B, U2.B
  N3: Part1.D4, U1.C, U2.C
  N4: Part1.D9, SP1.-
  N5: Part1.D10, microSD1.CS
  N6: Part1.D11/MOSI, microSD1.MOSI
  N7: Part1.D12/MISO, microSD1.MISO
  VDD: Part1.5V, U1.VDD, microSD1.VCC, U2.VDD, S1.Pin_3, S1.Pin_4, S2.Pin_3, S2.Pin_4, S3.Pin_3, S3.Pin_4, S4.Pin_3, S4.Pin_4, S5.Pin_3, S5.Pin_4, S6.Pin_3, S6.Pin_4, S7.Pin_3, S7.Pin_4, S8.Pin_3, S8.Pin_4
  N8: Part1.A1, U2.IO
  N9: Part1.A0, U1.IO
  N10: Part1.D13/SCK, microSD1.SCK
  N11: U1.IO4, S2.Pin_1, S2.Pin_2
  N12: U1.IO6, S4.Pin_1, S4.Pin_2
  N13: U1.IO7, S8.Pin_1, S8.Pin_2
  N14: U1.IO5, S3.Pin_1
  N15: U1.IO3, S1.Pin_1, S1.Pin_2
  N16: U1.IO0, S7.Pin_1, S7.Pin_2
  N17: U1.IO1, S6.Pin_1, S6.Pin_2
  N18: U1.IO2, S5.Pin_2
  N19: U2.IO4, LED2.anode
  N20: U2.IO6, LED4.anode
  N21: U2.IO7, LED8.anode
  N22: U2.IO5, LED3.anode
  N23: U2.IO3, LED1.anode
  N24: U2.IO0, LED7.anode
  N25: U2.IO1, LED6.anode
  N26: U2.IO2, LED5.anode
